// Logisim project ALU.circ as structural Verilog: 1 circuit, main circuit ALU
module ALU (
  input  [31:0] A,
  input  [31:0] B,
  input  [3:0] Codop,
  input  [4:0] Shift,
  input  CarryIn,
  output [31:0] S,
  output [3:0] Flags
);

  wire ADCm, ADCp, Am, Ap, Bm, Bp, CADC, CASR, CCMN, CCMP, CLSL, CMNm, CMNp, CMPm, CMPp, CROR, CSBC,
       not_1_out, SBCm, SBCp, subtractor_1_bout, subtractor_2_bout, VADC, VADC1, VADC2, VCMN, VCMN1, VCMN2,
       VCMP, VCMP1, VCMP2, VSBC, VSBC1, VSBC2;
  wire [4:0] negator_2_out, subtractor_3_out;
  wire [31:0] ADC, AND, ASR, BIC, CMN, CMP, EOR, LSL, LSR, MUL, MVN, not_3_out, ORR, ROR, SBC;

  assign AND = A & B;  // AND_Gate and_1, 32 bits wide
  assign EOR = A ^ B;  // XOR_Gate xor_1, 32 bits wide
  Shifter #(.width(32)) shifter_1 (.in(B), .\dist (Shift), .out(LSL));
  Shifter #(.width(32), .shift("lr")) shifter_2 (.in(B), .\dist (Shift), .out(LSR));
  Shifter #(.width(32), .shift("ar")) shifter_3 (.in(B), .\dist (Shift), .out(ASR));
  Adder #(.width(32)) adder_1 (.a(A), .b(B), .out(ADC), .cin(CarryIn), .cout(CADC));
  not not_1 (not_1_out, CarryIn);
  Subtractor #(.width(32)) subtractor_1 (.a(A), .b(B), .out(SBC), .bin(not_1_out), .bout(subtractor_1_bout));
  Shifter #(.width(32), .shift("rr")) shifter_4 (.in(A), .\dist (Shift), .out(ROR));
  Multiplexer #(.select(4), .width(32), .enable("false")) multiplexer_1 (
    .in0(AND), .in1(EOR), .in2(LSL), .in3(LSR), .in4(ASR), .in5(ADC), .in6(SBC), .in7(ROR), .in8(B), .in9(A),
    .in10(B), .in11(B), .in12(ORR), .in13(MUL), .in14(BIC), .in15(MVN), .out(S), .sel(Codop));
  not not_2 (CSBC, subtractor_1_bout);
  assign ORR = A | B;  // OR_Gate or_1, 32 bits wide
  Multiplier #(.width(32)) multiplier_1 (.a(A), .b(B), .out(MUL));  // open: cin, cout
  assign BIC = A & not_3_out;  // AND_Gate and_2, 32 bits wide
  assign not_3_out = ~B;  // NOT_Gate not_3, 32 bits wide
  assign MVN = ~B;  // NOT_Gate not_4, 32 bits wide
  Negator #(.width(32)) negator_1 ();  // open: in, out
  Adder #(.width(32)) adder_2 (.a(A), .b(B), .out(CMN), .cin(1'b0), .cout(CCMN));
  Subtractor #(.width(32)) subtractor_2 (.a(A), .b(B), .out(CMP), .bin(1'b0), .bout(subtractor_2_bout));
  not not_5 (CCMP, subtractor_2_bout);
  Comparator #(.width(32)) comparator_1 (.a(S), .b({32{1'b0}}), .eq(Flags[1]), .lt(Flags[0]));  // open: gt
  Subtractor #(.width(5)) subtractor_3 (.a(Shift), .b(5'b00001), .out(subtractor_3_out), .bin(1'b0));  // open: bout
  Negator #(.width(5)) negator_2 (.in(Shift), .out(negator_2_out));
  Multiplexer #(.select(4), .enable("false")) multiplexer_2 (
    .in0(1'b0), .in1(1'b0), .in2(CLSL), .in3(CASR), .in4(CASR), .in5(CADC), .in6(CSBC), .in7(CROR),
    .in8(1'b0), .in9(1'b0), .in10(CCMP), .in11(CCMN), .in12(1'b0), .in13(1'b0), .in14(1'b0), .in15(1'b0),
    .out(Flags[2]), .sel(Codop));
  BitSelector #(.width(32)) bitselector_1 (.in(B), .out(CLSL), .sel(negator_2_out));
  BitSelector #(.width(32)) bitselector_2 (.in(B), .out(CROR), .sel({5{1'b1}}));
  BitSelector #(.width(32)) bitselector_3 (.in(B), .out(CASR), .sel(subtractor_3_out));
  Comparator #(.width(32)) comparator_2 (.a(ADC), .b({32{1'b0}}), .gt(ADCp), .lt(ADCm));  // open: eq
  Comparator #(.width(32)) comparator_3 (.a(A), .b({32{1'b0}}), .gt(Ap), .lt(Am));  // open: eq
  Comparator #(.width(32)) comparator_4 (.a(B), .b({32{1'b0}}), .gt(Bp), .lt(Bm));  // open: eq
  Comparator #(.width(32)) comparator_5 (.a(SBC), .b({32{1'b0}}), .gt(SBCp), .lt(SBCm));  // open: eq
  and and_3 (VADC1, Ap, Bp, ADCm);
  and and_4 (VSBC1, Am, Bp, SBCm);
  and and_5 (VCMN1, Ap, Bp, CMNm);
  and and_6 (VCMP1, Am, Bp, CMPm);
  Multiplexer #(.select(4), .enable("false")) multiplexer_3 (
    .in0(1'b0), .in1(1'b0), .in2(1'b0), .in3(1'b0), .in4(1'b0), .in5(VADC), .in6(VSBC), .in7(1'b0),
    .in8(1'b0), .in9(1'b0), .in10(VCMP), .in11(VCMN), .in12(1'b0), .in13(1'b0), .in14(1'b0), .in15(1'b0),
    .out(Flags[3]), .sel(Codop));
  Comparator #(.width(32)) comparator_6 (.a(CMN), .b({32{1'b0}}), .gt(CMNp), .lt(CMNm));  // open: eq
  Comparator #(.width(32)) comparator_7 (.a(CMP), .b({32{1'b0}}), .gt(CMPp), .lt(CMPm));  // open: eq
  and and_7 (VADC2, Am, Bm, ADCp);
  and and_8 (VSBC2, Ap, Bm, SBCp);
  and and_9 (VCMN2, Am, Bm, CMNp);
  and and_10 (VCMP2, Ap, Bm, CMPp);
  or or_2 (VADC, VADC1, VADC2);
  or or_3 (VSBC, VSBC1, VSBC2);
  or or_4 (VCMN, VCMN1, VCMN2);
  or or_5 (VCMP, VCMP1, VCMP2);

  // Other names for the same wires on the sheet: CLSR = CASR; N = Flags[0]; Z = Flags[1]; C = Flags[2]; V = Flags[3];
  //   RSB[31:0] = A; TST[31:0] = AND

  // Notes on the sheet:
  //   Note: for ROR, C = N
  //   Note 2: assume that shift > 0 for LSL and LSR
endmodule
