// Logisim project Controller.circ as structural Verilog: 8 circuits, main circuit Controller
module Controller (
  input  [15:0] Inst,
  input  Clk,
  input  Reset,
  input  [3:0] Flags,
  output Carry,
  output DP_Shift,
  output Imm32_Enable,
  output [4:0] Imm5,
  output [31:0] Imm32,
  output [3:0] ALU_Opcode,
  output [2:0] Rm,
  output [2:0] Rn,
  output [2:0] Rd,
  output [31:0] RAM_Addr,
  output Load,
  output Store,
  output [7:0] PC
);

  wire Conditional_1_verified, Load_Store_1_pc_hold, not_1_out, Opcode_Decoder_1_conditional,
       Opcode_Decoder_1_data_processing, Opcode_Decoder_1_load_store, Opcode_Decoder_1_shift,
       Opcode_Decoder_1_sp_address, Shift_Add_Sub_Mov_1_carry, SP_Address_1_write_enable;
  wire [2:0] Data_Processing_1_p4, Data_Processing_1_p5, Data_Processing_1_p6, Load_Store_1_rd,
       Load_Store_1_rm, Shift_Add_Sub_Mov_1_rd, Shift_Add_Sub_Mov_1_rm, Shift_Add_Sub_Mov_1_rn;
  wire [3:0] Data_Processing_1_p3, Data_Processing_1_p7, flags_apsr_1_flags_out, or_1_out,
       Shift_Add_Sub_Mov_1_alu_opcode, Shift_Add_Sub_Mov_1_flags_update_mask;
  wire [7:0] adder_1_out, adder_2_out, Conditional_1_offset;
  wire [31:0] SP_Address_1_new_stack_pointer, Stack_Pointer_q;

  Register #(.width(32)) Stack_Pointer (
    .D(SP_Address_1_new_stack_pointer), .en(SP_Address_1_write_enable), .clk(Clk), .Q(Stack_Pointer_q),
    .clr(Reset));
  Opcode_Decoder Opcode_Decoder_1 (
    .Opcode(Inst[15:10]), .Shift(Opcode_Decoder_1_shift), .Data_Processing(Opcode_Decoder_1_data_processing),
    .Load_Store(Opcode_Decoder_1_load_store), .SP_Address(Opcode_Decoder_1_sp_address),
    .Conditional(Opcode_Decoder_1_conditional));
  assign or_1_out = Data_Processing_1_p7 | Shift_Add_Sub_Mov_1_flags_update_mask;  // OR_Gate or_1, 4 bits wide
  Shift_Add_Sub_Mov Shift_Add_Sub_Mov_1 (
    .Imm32_Enable(Imm32_Enable), .ALU_Opcode(Shift_Add_Sub_Mov_1_alu_opcode), .Instruction(Inst),
    .Enable(Opcode_Decoder_1_shift), .Carry(Shift_Add_Sub_Mov_1_carry),
    .Flags_Update_Mask(Shift_Add_Sub_Mov_1_flags_update_mask), .Rd(Shift_Add_Sub_Mov_1_rd),
    .Rn(Shift_Add_Sub_Mov_1_rn), .Rm(Shift_Add_Sub_Mov_1_rm), .Imm5(Imm5), .Imm32(Imm32));
  // Data_Processing Data_Processing_1: pin names not known; wires that end beside it: Inst, Opcode_Decoder_1_data_processing, Data_Processing_1_p3, Data_Processing_1_p4, Data_Processing_1_p5, Data_Processing_1_p6, Data_Processing_1_p7
  Flags_APSR flags_apsr_1 (
    .Clk(Clk), .Rst(Reset), .Flags_In(or_1_out), .Update_Mask(Flags), .Flags_Out(flags_apsr_1_flags_out));
  Load_Store Load_Store_1 (
    .Load(Load), .Store(Store), .Enable(Opcode_Decoder_1_load_store), .Rm(Load_Store_1_rm),
    .Rd(Load_Store_1_rd), .Stack_Pointer(Stack_Pointer_q), .RAM_Addr(RAM_Addr), .Instruction(Inst),
    .Clk(Clk), .Reset(Reset), .PC_Hold(Load_Store_1_pc_hold));
  Conditional Conditional_1 (
    .Enable(Opcode_Decoder_1_conditional), .Instruction(Inst), .N(flags_apsr_1_flags_out[3]),
    .Z(flags_apsr_1_flags_out[2]), .C(flags_apsr_1_flags_out[1]), .V(flags_apsr_1_flags_out[0]),
    .Offset(Conditional_1_offset), .Verified(Conditional_1_verified));
  SP_Address SP_Address_1 (
    .New_Stack_Pointer(SP_Address_1_new_stack_pointer), .Enable(Opcode_Decoder_1_sp_address),
    .Write_Enable(SP_Address_1_write_enable), .Instruction(Inst), .Stack_Pointer(Stack_Pointer_q));
  Adder adder_1 (.a(8'h3), .b(Conditional_1_offset), .out(adder_1_out), .cin(1'b0));  // open: cout
  Adder adder_2 (.a(adder_1_out), .b(PC), .out(adder_2_out), .cin(1'b0));  // open: cout
  and and_1 (DP_Shift, Opcode_Decoder_1_shift, ~Opcode_Decoder_1_data_processing);  // AND_Gate
  not not_1 (not_1_out, Load_Store_1_pc_hold);
  Counter counter_1 (
    .clr(Reset), .load(Conditional_1_verified), .up(1'b1), .count(not_1_out), .clk(Clk), .D(adder_2_out),
    .Q(PC));  // open: carry
  Multiplexer #(.enable("false")) multiplexer_1 (
    .in0(flags_apsr_1_flags_out[1]), .in1(Shift_Add_Sub_Mov_1_carry), .out(Carry), .sel(DP_Shift));
  assign ALU_Opcode = Shift_Add_Sub_Mov_1_alu_opcode | Data_Processing_1_p3;  // OR_Gate or_2, 4 bits wide
  assign Rm = Shift_Add_Sub_Mov_1_rm | Data_Processing_1_p4 | Load_Store_1_rm;  // OR_Gate or_3, 3 bits wide
  assign Rn = Shift_Add_Sub_Mov_1_rn | Data_Processing_1_p5;  // OR_Gate or_4, 3 bits wide
  assign Rd = Shift_Add_Sub_Mov_1_rd | Data_Processing_1_p6 | Load_Store_1_rd;  // OR_Gate or_5, 3 bits wide

  // Notes on the sheet:
  //   Extract carry
  //   Extract Opcode
  //   IF Reg_Imm=1 THEN use shift value from register ELSE use shift value from Imm5
  //   Buffer flags for next instruction
  //   Add 3 to offset because ARM pre-increments PC
  //   and does an additionnal prefect operation
endmodule

module Conditional (
  input  Enable,
  input  [15:0] Instruction,
  input  N,
  input  Z,
  input  C,
  input  V,
  output [7:0] Offset,
  output Verified
);

  wire and_2_out, and_3_out, and_4_out, comparator_1_eq, comparator_2_eq, comparator_3_eq, comparator_4_eq,
       comparator_5_eq, comparator_6_eq, comparator_7_eq, comparator_8_eq, comparator_9_eq, comparator_10_eq,
       not_1_out, not_2_out, or_1_out;
  wire [15:0] bit_extender_1_out;
  wire [15:8] and_1_out;

  assign bit_extender_1_out = {{15{Enable}}, Enable};  // Bit_Extender bit_extender_1
  assign {and_1_out, Offset} = bit_extender_1_out & Instruction;  // AND_Gate and_1, 16 bits wide
  Comparator #(.width(1)) comparator_1 (.a(Z), .b(1'b1), .eq(comparator_1_eq));  // open: gt, lt
  Comparator #(.width(1)) comparator_2 (.a(Z), .b(1'b0), .eq(comparator_2_eq));  // open: gt, lt
  Comparator #(.width(1)) comparator_3 (.a(C), .b(1'b1), .eq(comparator_3_eq));  // open: gt, lt
  Comparator #(.width(1)) comparator_4 (.a(C), .b(1'b0), .eq(comparator_4_eq));  // open: gt, lt
  Comparator #(.width(1)) comparator_5 (.a(N), .b(1'b1), .eq(comparator_5_eq), .lt(comparator_5_eq));  // open: gt
  Comparator #(.width(1)) comparator_6 (.a(N), .b(1'b0), .eq(comparator_6_eq));  // open: gt, lt
  Comparator #(.width(1)) comparator_7 (.a(V), .b(1'b1), .eq(comparator_7_eq));  // open: gt, lt
  Comparator #(.width(1)) comparator_8 (.a(V), .b(1'b0), .eq(comparator_8_eq));  // open: gt, lt
  Comparator #(.width(1)) comparator_9 (.a(N), .b(V), .eq(comparator_9_eq));  // open: gt, lt
  Comparator #(.width(1)) comparator_10 (.a(V), .b(Z), .eq(comparator_10_eq));  // open: gt, lt
  not not_1 (not_1_out, comparator_9_eq);
  not not_2 (not_2_out, comparator_10_eq);
  and and_2 (and_2_out, comparator_2_eq, comparator_3_eq);
  and and_3 (and_3_out, comparator_2_eq, comparator_9_eq);
  or or_1 (or_1_out, comparator_1_eq, not_2_out);
  and and_4 (and_4_out, comparator_4_eq, comparator_1_eq);
  Multiplexer #(.select(4), .enable("false")) multiplexer_1 (
    .in0(comparator_1_eq), .in1(comparator_2_eq), .in2(comparator_3_eq), .in3(comparator_4_eq),
    .in4(comparator_5_eq), .in5(comparator_6_eq), .in6(comparator_7_eq), .in7(comparator_8_eq),
    .in8(and_2_out), .in9(and_4_out), .in10(comparator_9_eq), .in11(not_1_out), .in12(and_3_out),
    .in13(or_1_out), .in14(1'b1), .out(Verified), .sel(and_1_out[11:8]));  // open: in15
endmodule

module Opcode_Decoder (
  input  [5:0] Opcode,
  output Shift,
  output Data_Processing,
  output Load_Store,
  output SP_Address,
  output Conditional
);

  wire comparator_2_eq, comparator_2_lt, comparator_3_eq, comparator_3_gt, comparator_4_eq, comparator_4_gt,
       comparator_5_eq, comparator_5_lt, comparator_6_eq, comparator_6_gt, comparator_7_eq, comparator_7_lt,
       comparator_8_eq, comparator_8_lt, comparator_9_eq, comparator_9_gt, or_1_out, or_2_out, or_3_out,
       or_4_out, or_5_out, or_6_out, or_7_out, or_8_out;

  Comparator #(.width(6)) comparator_1 (.a(Opcode), .b(6'b010000), .eq(Data_Processing));  // open: gt, lt
  Comparator #(.width(6)) comparator_2 (
    .a(Opcode), .b(6'b100111), .eq(comparator_2_eq), .lt(comparator_2_lt));  // open: gt
  Comparator #(.width(6)) comparator_3 (
    .a(Opcode), .b(6'b100100), .gt(comparator_3_gt), .eq(comparator_3_eq));  // open: lt
  Comparator #(.width(6)) comparator_4 (
    .a(Opcode), .b(6'b101100), .gt(comparator_4_gt), .eq(comparator_4_eq));  // open: lt
  Comparator #(.width(6)) comparator_5 (
    .a(Opcode), .b(6'b101111), .eq(comparator_5_eq), .lt(comparator_5_lt));  // open: gt
  Comparator #(.width(6)) comparator_6 (
    .a(Opcode), .b(6'b110100), .gt(comparator_6_gt), .eq(comparator_6_eq));  // open: lt
  Comparator #(.width(6)) comparator_7 (
    .a(Opcode), .b(6'b110111), .eq(comparator_7_eq), .lt(comparator_7_lt));  // open: gt
  Comparator #(.width(6)) comparator_8 (
    .a(Opcode), .b(6'b001111), .eq(comparator_8_eq), .lt(comparator_8_lt));  // open: gt
  Comparator #(.width(6)) comparator_9 (
    .a(Opcode), .b({6{1'b0}}), .gt(comparator_9_gt), .eq(comparator_9_eq));  // open: lt
  or or_1 (or_1_out, comparator_2_eq, comparator_2_lt);
  or or_2 (or_2_out, comparator_3_gt, comparator_3_eq);
  or or_3 (or_3_out, comparator_4_gt, comparator_4_eq);
  or or_4 (or_4_out, comparator_5_eq, comparator_5_lt);
  or or_5 (or_5_out, comparator_6_gt, comparator_6_eq);
  or or_6 (or_6_out, comparator_7_eq, comparator_7_lt);
  or or_7 (or_7_out, comparator_8_eq, comparator_8_lt);
  or or_8 (or_8_out, comparator_9_gt, comparator_9_eq);
  and and_1 (Load_Store, or_1_out, or_2_out);
  and and_2 (SP_Address, or_3_out, or_4_out);
  and and_3 (Conditional, or_5_out, or_6_out);
  and and_4 (Shift, or_7_out, or_8_out);

  // Notes on the sheet:
  //   Data Processing
  //   Load/Store
  //   SP Address
  //   Conditional branch
  //   Shift, add, sub, mov
endmodule

module Data_Processing (
  input  [15:0] Instruction,
  input  Enable,
  output [2:0] Rn,
  output [2:0] Rd,
  output [2:0] Rm,
  output [3:0] ALU_Opcode,
  output [3:0] Flags_Update_Mask
);

  wire [15:0] bit_extender_1_out;
  wire [15:10] and_1_out;

  assign bit_extender_1_out = {{15{Enable}}, Enable};  // Bit_Extender bit_extender_1
  assign {and_1_out, ALU_Opcode, Rm, Rd} = Instruction & bit_extender_1_out;  // AND_Gate and_1, 16 bits wide
  Multiplexer #(.select(4), .width(4), .enable("false")) multiplexer_1 (
    .in0(4'b1000), .in1(4'b1000), .in2(4'b1000), .in3(4'b1000), .in4(4'b1000), .in5(4'b0000), .in6(4'b0000),
    .in7(4'b1000), .in8(4'b1000), .in9(4'b0000), .in10(4'b0000), .in11(4'b0000), .in12(4'b1000),
    .in13(4'b1100), .in14(4'b1000), .in15(4'b1000), .out(Flags_Update_Mask), .sel(ALU_Opcode));

  assign Rn = Rd;

  // Notes on the sheet:
  //   Note 2: RSB instruction has Rn as 1st operand.
  //   MUL instruction has Rn as 1st operand and Rdm as 2nd operand
  //   For simplification purposes, Rm is used for 1st operand both here and in the ALU.
  //   Note: instructions that does not save the result will still have the second operand as the destination register, the ALU will copy the second register to the destination register
  //   Pull output low on Enable = 0
endmodule

module Shift_Add_Sub_Mov (
  input  [15:0] Instruction,
  input  Enable,
  output [3:0] ALU_Opcode,
  output [2:0] Rm,
  output [2:0] Rn,
  output [2:0] Rd,
  output [4:0] Imm5,
  output Imm32_Enable,
  output Carry,
  output [31:0] Imm32,
  output [3:0] Flags_Update_Mask
);

  wire comparator_1_eq, comparator_2_eq, comparator_3_eq, comparator_4_eq, comparator_5_eq, comparator_6_eq,
       comparator_7_eq, comparator_8_eq;
  wire [2:0] and_1_out_2, bit_extender_2_out, bit_extender_3_out, bit_extender_4_out, bit_extender_5_out,
       bit_extender_6_out, bit_extender_7_out, bit_extender_8_out, bit_extender_9_out, multiplexer_1_out,
       multiplexer_2_out, multiplexer_3_out, multiplexer_4_out, multiplexer_5_out, multiplexer_6_out,
       multiplexer_7_out, or_1_out;
  wire [3:0] multiplexer_8_out, multiplexer_9_out, multiplexer_10_out, multiplexer_19_out,
       multiplexer_20_out, multiplexer_21_out, multiplexer_22_out, multiplexer_23_out;
  wire [15:0] and_1_out, bit_extender_1_out;
  wire [31:0] bit_extender_10_out, bit_extender_11_out;

  assign bit_extender_1_out = {{15{Enable}}, Enable};  // Bit_Extender bit_extender_1
  Comparator #(.width(3)) comparator_1 (.a(and_1_out_2), .b(3'b000), .eq(comparator_1_eq));  // open: gt, lt
  Comparator #(.width(3)) comparator_2 (.a(and_1_out_2), .b(3'b001), .eq(comparator_2_eq));  // open: gt, lt
  Comparator #(.width(3)) comparator_3 (.a(and_1_out_2), .b(3'b010), .eq(comparator_3_eq));  // open: gt, lt
  Comparator #(.width(5)) comparator_4 (
    .a({and_1_out_2, and_1_out[10:9]}), .b(5'b01100), .eq(comparator_4_eq));  // open: gt, lt
  Comparator #(.width(5)) comparator_5 (
    .a({and_1_out_2, and_1_out[10:9]}), .b(5'b01101), .eq(comparator_5_eq));  // open: gt, lt
  Comparator #(.width(5)) comparator_6 (
    .a({and_1_out_2, and_1_out[10:9]}), .b(5'b01110), .eq(comparator_6_eq));  // open: gt, lt
  Comparator #(.width(5)) comparator_7 (
    .a({and_1_out_2, and_1_out[10:9]}), .b(5'b01111), .eq(comparator_7_eq));  // open: gt, lt
  Comparator #(.width(3)) comparator_8 (.a(and_1_out_2), .b(3'b100), .eq(comparator_8_eq));  // open: gt, lt
  assign {and_1_out[15:14], and_1_out_2, and_1_out[10:0]} = Instruction & bit_extender_1_out;  // AND_Gate and_1, 16 bits wide
  assign bit_extender_2_out = {{2{1'b0}}, comparator_1_eq};  // Bit_Extender bit_extender_2
  assign bit_extender_3_out = {{2{1'b0}}, comparator_2_eq};  // Bit_Extender bit_extender_3
  assign bit_extender_4_out = {{2{1'b0}}, comparator_3_eq};  // Bit_Extender bit_extender_4
  assign bit_extender_5_out = {{2{1'b0}}, comparator_4_eq};  // Bit_Extender bit_extender_5
  assign bit_extender_6_out = {{2{1'b0}}, comparator_5_eq};  // Bit_Extender bit_extender_6
  assign bit_extender_7_out = {{2{1'b0}}, comparator_6_eq};  // Bit_Extender bit_extender_7
  assign bit_extender_8_out = {{2{1'b0}}, comparator_7_eq};  // Bit_Extender bit_extender_8
  assign bit_extender_9_out = {{2{1'b0}}, comparator_8_eq};  // Bit_Extender bit_extender_9
  Multiplexer #(.width(3), .enable("false")) multiplexer_1 (
    .in0(bit_extender_2_out), .in1(3'b000), .out(multiplexer_1_out), .sel(comparator_1_eq));
  Multiplexer #(.width(3), .enable("false")) multiplexer_2 (
    .in0(bit_extender_4_out), .in1(3'b010), .out(multiplexer_2_out), .sel(comparator_3_eq));
  Multiplexer #(.width(3), .enable("false")) multiplexer_3 (
    .in0(bit_extender_5_out), .in1(3'b011), .out(multiplexer_3_out), .sel(comparator_4_eq));
  Multiplexer #(.width(3), .enable("false")) multiplexer_4 (
    .in0(bit_extender_6_out), .in1(3'b100), .out(multiplexer_4_out), .sel(comparator_5_eq));
  Multiplexer #(.width(3), .enable("false")) multiplexer_5 (
    .in0(bit_extender_7_out), .in1(3'b101), .out(multiplexer_5_out), .sel(comparator_6_eq));
  Multiplexer #(.width(3), .enable("false")) multiplexer_6 (
    .in0(bit_extender_8_out), .in1(3'b110), .out(multiplexer_6_out), .sel(comparator_7_eq));
  Multiplexer #(.width(3), .enable("false")) multiplexer_7 (
    .in0(bit_extender_9_out), .in1(3'b111), .out(multiplexer_7_out), .sel(comparator_8_eq));
  assign bit_extender_10_out = {{24{1'b0}}, and_1_out[7:0]};  // Bit_Extender bit_extender_10
  assign or_1_out = multiplexer_1_out | bit_extender_3_out | multiplexer_2_out | multiplexer_3_out | multiplexer_4_out | multiplexer_5_out | multiplexer_6_out | multiplexer_7_out;  // OR_Gate or_1, 3 bits wide
  Multiplexer #(.width(4), .enable("false")) multiplexer_8 (
    .in0(4'b0000), .in1(4'b0100), .out(multiplexer_8_out), .sel(Enable));
  Multiplexer #(.width(4), .enable("false")) multiplexer_9 (
    .in0(4'b0000), .in1(4'b0101), .out(multiplexer_9_out), .sel(Enable));
  Multiplexer #(.width(4), .enable("false")) multiplexer_10 (
    .in0(4'b0000), .in1(4'b0101), .out(multiplexer_10_out), .sel(Enable));
  Multiplexer #(.select(3), .width(3), .enable("false")) multiplexer_11 (
    .in0(and_1_out[5:3]), .in1(and_1_out[5:3]), .in2(and_1_out[5:3]), .in3(and_1_out[8:6]),
    .in4(and_1_out[8:6]), .in5(3'b000), .in6(3'b000), .in7(3'b000), .out(Rm), .sel(or_1_out));
  Multiplexer #(.select(3), .width(3), .enable("false")) multiplexer_12 (
    .in0(3'b000), .in1(3'b000), .in2(3'b000), .in3(and_1_out[5:3]), .in4(and_1_out[5:3]),
    .in5(and_1_out[5:3]), .in6(and_1_out[5:3]), .in7(3'b000), .out(Rn), .sel(or_1_out));
  Multiplexer #(.select(3), .width(3), .enable("false")) multiplexer_13 (
    .in0(and_1_out[2:0]), .in1(and_1_out[2:0]), .in2(and_1_out[2:0]), .in3(and_1_out[2:0]),
    .in4(and_1_out[2:0]), .in5(and_1_out[2:0]), .in6(and_1_out[2:0]), .in7(and_1_out[10:8]), .out(Rd),
    .sel(or_1_out));
  Multiplexer #(.select(3), .width(5), .enable("false")) multiplexer_14 (
    .in0(and_1_out[10:6]), .in1(and_1_out[10:6]), .in2(and_1_out[10:6]), .in3({5{1'b0}}), .in4({5{1'b0}}),
    .in5({5{1'b0}}), .in6({5{1'b0}}), .in7({5{1'b0}}), .out(Imm5), .sel(or_1_out));
  Multiplexer #(.select(3), .enable("false")) multiplexer_15 (
    .in0(1'b0), .in1(1'b0), .in2(1'b0), .in3(1'b0), .in4(1'b0), .in5(1'b1), .in6(1'b1), .in7(1'b1),
    .out(Imm32_Enable), .sel(or_1_out));
  Multiplexer #(.select(3), .enable("false")) multiplexer_16 (
    .in0(1'b0), .in1(1'b0), .in2(1'b0), .in3(1'b0), .in4(1'b0), .in5(1'b0), .in6(1'b1), .in7(1'b0),
    .out(Carry), .sel(or_1_out));
  assign bit_extender_11_out = {{29{1'b0}}, and_1_out[8:6]};  // Bit_Extender bit_extender_11
  Multiplexer #(.select(3), .width(32), .enable("false")) multiplexer_17 (
    .in0({32{1'b0}}), .in1({32{1'b0}}), .in2({32{1'b0}}), .in3({32{1'b0}}), .in4({32{1'b0}}),
    .in5(bit_extender_11_out), .in6(bit_extender_11_out), .in7(bit_extender_10_out), .out(Imm32),
    .sel(or_1_out));
  Multiplexer #(.select(3), .width(4), .enable("false")) multiplexer_18 (
    .in0(4'b1110), .in1(4'b1110), .in2(4'b1110), .in3(4'b1111), .in4(4'b1111), .in5(4'b1111), .in6(4'b1111),
    .in7(4'b1100), .out(Flags_Update_Mask), .sel(or_1_out));
  Multiplexer #(.width(4), .enable("false")) multiplexer_19 (
    .in0(4'b0000), .in1(4'b0010), .out(multiplexer_19_out), .sel(Enable));
  Multiplexer #(.width(4), .enable("false")) multiplexer_20 (
    .in0(4'b0000), .in1(4'b0011), .out(multiplexer_20_out), .sel(Enable));
  Multiplexer #(.width(4), .enable("false")) multiplexer_21 (
    .in0(4'b0000), .in1(4'b0110), .out(multiplexer_21_out), .sel(Enable));
  Multiplexer #(.width(4), .enable("false")) multiplexer_22 (
    .in0(4'b0000), .in1(4'b1001), .out(multiplexer_22_out), .sel(Enable));
  Multiplexer #(.width(4), .enable("false")) multiplexer_23 (
    .in0(4'b0000), .in1(4'b0110), .out(multiplexer_23_out), .sel(Enable));
  Multiplexer #(.select(3), .width(4), .enable("false")) multiplexer_24 (
    .in0(multiplexer_19_out), .in1(multiplexer_20_out), .in2(multiplexer_8_out), .in3(multiplexer_9_out),
    .in4(multiplexer_23_out), .in5(multiplexer_10_out), .in6(multiplexer_21_out), .in7(multiplexer_22_out),
    .out(ALU_Opcode), .sel(or_1_out));

  // Notes on the sheet:
  //   Pull output low on Enable = 0
  //   Note 3: Imm32_Enable forces the use of the immediate for Rm register
  //   CAS LSL
  //   CAS LSR
  //   CAS ASR
  //   CAS ADD REG
  //   CAS SUB REG
  //   CAS ADD
  //   CAS SUB
  //   CAS MOV
  //   Note: ALU uses Rn register for shifts. Use Rn instead of Rm for shifts (immediate) here too
  //   Note 2: MOV uses RSB ALU opcode with Imm8 reversed so that it is copied to output register
  //   ALU will use Imm32 instead of Rm
  //   Enable carry for SUB since it is reversed in ALU
endmodule

module Load_Store (
  input  [15:0] Instruction,
  input  [31:0] Stack_Pointer,
  input  Enable,
  input  Clk,
  input  Reset,
  output Store,
  output Load,
  output PC_Hold,
  output [2:0] Rd,
  output [2:0] Rm,
  output [31:0] RAM_Addr
);

  wire and_1_out, comparator_1_eq, comparator_1_lt, not_1_out;
  wire [31:0] bit_extender_1_out;

  assign bit_extender_1_out = {{24{1'b0}}, Instruction[7:0]};  // Bit_Extender bit_extender_1
  Comparator #(.width(1)) comparator_1 (
    .a(Instruction[11]), .b(1'b0), .eq(comparator_1_eq), .lt(comparator_1_lt));  // open: gt
  Adder #(.width(32)) adder_1 (.a(bit_extender_1_out), .b(Stack_Pointer), .out(RAM_Addr));  // open: cin, cout
  Multiplexer #(.enable("false")) multiplexer_1 (.in0(Enable), .in1(comparator_1_eq), .out(Store), .sel(Enable));
  Multiplexer #(.enable("false")) multiplexer_2 (.in0(Enable), .in1(comparator_1_lt), .out(Load), .sel(Enable));
  and and_1 (and_1_out, Load, not_1_out);
  D_Flip_Flop d_ff_1 (.D(and_1_out), .clk(Clk), .Q(PC_Hold), .reset(Reset));  // open: Qn, preset
  not not_1 (not_1_out, PC_Hold);

  assign Rd = Instruction[10:8];
  assign Rm = Instruction[10:8];

  // Notes on the sheet:
  //   Delay load and hold PC for 1 cycle for the RAM to send out requested data 
endmodule

module SP_Address (
  input  Enable,
  input  [15:0] Instruction,
  input  [31:0] Stack_Pointer,
  output Write_Enable,
  output [31:0] New_Stack_Pointer
);

  wire [6:0] and_1_out;
  wire [15:0] bit_extender_1_out;
  wire [15:7] and_1_out_2;
  wire [31:0] adder_1_out, bit_extender_2_out, subtractor_1_out;

  assign bit_extender_1_out = {{15{Enable}}, Enable};  // Bit_Extender bit_extender_1
  assign bit_extender_2_out = {{25{and_1_out[6]}}, and_1_out};  // Bit_Extender bit_extender_2
  assign {and_1_out_2, and_1_out} = bit_extender_1_out & Instruction;  // AND_Gate and_1, 16 bits wide
  Adder #(.width(32)) adder_1 (.a(bit_extender_2_out), .b(Stack_Pointer), .out(adder_1_out));  // open: cin, cout
  Subtractor #(.width(32)) subtractor_1 (
    .a(bit_extender_2_out), .b(Stack_Pointer), .out(subtractor_1_out));  // open: bin, bout
  Multiplexer #(.width(32), .enable("false")) multiplexer_1 (
    .in0(adder_1_out), .in1(subtractor_1_out), .out(New_Stack_Pointer), .sel(and_1_out_2[7]));

  assign Write_Enable = Enable;

  // Notes on the sheet:
  //   Pull output low on Enable = 0
endmodule

module Flags_APSR (
  input  Clk,
  input  Rst,
  input  [3:0] Flags_In,
  input  [3:0] Update_Mask,
  output [3:0] Flags_Out
);

  wire [3:0] register_1_q;

  Register #(.width(4)) register_1 (.D(Flags_Out), .en(1'b1), .clk(Clk), .Q(register_1_q), .clr(Rst));
  Multiplexer #(.enable("false")) multiplexer_1 (
    .in0(register_1_q[0]), .in1(Flags_In[0]), .out(Flags_Out[0]), .sel(Update_Mask[0]));
  Multiplexer #(.enable("false")) multiplexer_2 (
    .in0(register_1_q[1]), .in1(Flags_In[1]), .out(Flags_Out[1]), .sel(Update_Mask[1]));
  Multiplexer #(.enable("false")) multiplexer_3 (
    .in0(register_1_q[2]), .in1(Flags_In[2]), .out(Flags_Out[2]), .sel(Update_Mask[2]));
  Multiplexer #(.enable("false")) multiplexer_4 (
    .in0(register_1_q[3]), .in1(Flags_In[3]), .out(Flags_Out[3]), .sel(Update_Mask[3]));
endmodule
