// Logisim project cadeux.circ as structural Verilog: 1 circuit, main circuit main
module main (
  input  [15:0] in_1,
  input  in_2,
  output [3:0] out_3,
  output [3:0] out_4,
  output [3:0] out_5,
  output [3:0] out_6,
  output [3:0] out_7,
  output [3:0] out_8,
  output [2:0] out_9,
  output [2:0] out_10,
  output [3:0] out_11,
  output [7:0] out_12,
  output [3:0] out_13,
  output out_14,
  output out_15,
  output [2:0] out_16,
  output [2:0] out_17,
  output [2:0] out_18,
  output [4:0] out_19,
  output [31:0] out_20
);

  wire comparator_1_eq, comparator_2_eq, comparator_3_eq, comparator_4_eq, comparator_5_eq, comparator_6_eq,
       comparator_7_eq, comparator_8_eq, not_1_out, or_1_out, or_2_out, or_3_out, or_5_out, or_9_out,
       or_10_out;
  wire [2:0] and_1_out, and_4_out, and_7_out, and_8_out, bit_extender_2_out, bit_extender_5_out,
       bit_extender_6_out, bit_extender_7_out, bit_extender_17_out, bit_extender_18_out, bit_extender_19_out,
       bitselector_3_out, bitselector_6_out, bitselector_8_out, bitselector_9_out, or_4_out, or_7_out;
  wire [3:0] bit_extender_3_out, bit_extender_10_out, bit_extender_11_out, bit_extender_12_out,
       bit_extender_13_out, bit_extender_14_out, bit_extender_15_out, or_8_out;
  wire [4:0] and_5_out, bit_extender_4_out, bit_extender_16_out, bitselector_10_out;
  wire [7:0] bit_extender_1_out, bitselector_12_out, not_2_out;
  wire [31:0] bit_extender_8_out, bit_extender_9_out;

  assign bit_extender_1_out = {{7{comparator_4_eq}}, comparator_4_eq};  // Bit_Extender bit_extender_1
  assign bit_extender_2_out = {{2{in_2}}, in_2};  // Bit_Extender bit_extender_2
  assign bit_extender_3_out = {{3{in_2}}, in_2};  // Bit_Extender bit_extender_3
  assign bit_extender_4_out = {{4{in_2}}, in_2};  // Bit_Extender bit_extender_4
  BitSelector #(.width(16)) bitselector_1 (.in(in_1), .out(bitselector_3_out[2]), .sel(4'b1101));
  BitSelector #(.width(16)) bitselector_2 (.in(in_1), .out(bitselector_3_out[1]), .sel(4'b1100));
  BitSelector #(.width(16)) bitselector_3 (.in(in_1), .out(bitselector_3_out[0]), .sel(4'b1011));
  BitSelector #(.width(16)) bitselector_4 (.in(in_1), .out(bitselector_10_out[4]), .sel(4'b1010));
  BitSelector #(.width(16)) bitselector_5 (.in(in_1), .out(bitselector_10_out[3]), .sel(4'b1001));
  BitSelector #(.width(16), .group(3)) bitselector_6 (.in(in_1), .out(bitselector_6_out), .sel(3'b000));
  BitSelector #(.width(16)) bitselector_7 (.in(in_1), .out(bitselector_10_out[2]), .sel(4'b1000));
  BitSelector #(.width(16), .group(3)) bitselector_8 (.in(in_1), .out(bitselector_8_out), .sel(3'b001));
  BitSelector #(.width(16), .group(3)) bitselector_9 (.in(in_1), .out(bitselector_9_out), .sel(3'b010));
  BitSelector #(.width(16)) bitselector_10 (.in(in_1), .out(bitselector_10_out[0]), .sel(4'b0110));
  BitSelector #(.width(16)) bitselector_11 (.in(in_1), .out(bitselector_10_out[1]), .sel(4'b0111));
  BitSelector #(.width(16), .group(8)) bitselector_12 (.in(in_1), .out(bitselector_12_out), .sel(1'b0));
  not not_1 (not_1_out, comparator_4_eq);
  or or_1 (or_1_out, or_3_out, or_5_out);
  assign bit_extender_5_out = {{2{or_1_out}}, or_1_out};  // Bit_Extender bit_extender_5
  assign and_1_out = bit_extender_18_out & bitselector_9_out;  // AND_Gate and_1, 3 bits wide
  assign out_12 = bitselector_12_out & bit_extender_1_out;  // AND_Gate and_2, 8 bits wide
  assign bit_extender_6_out = {{2{not_1_out}}, not_1_out};  // Bit_Extender bit_extender_6
  assign out_9 = bit_extender_5_out & bitselector_8_out;  // AND_Gate and_3, 3 bits wide
  assign and_4_out = bit_extender_17_out & bitselector_8_out;  // AND_Gate and_4, 3 bits wide
  assign and_5_out = bit_extender_16_out & bitselector_10_out;  // AND_Gate and_5, 5 bits wide
  assign out_10 = bit_extender_19_out & bitselector_10_out[2:0];  // AND_Gate and_6, 3 bits wide
  assign not_2_out = ~out_12;  // NOT_Gate not_2, 8 bits wide
  Comparator #(.width(3)) comparator_1 (.a(bitselector_3_out), .b(3'b000), .eq(comparator_1_eq));  // open: gt, lt
  Comparator #(.width(3)) comparator_2 (.a(bitselector_3_out), .b(3'b001), .eq(comparator_2_eq));  // open: gt, lt
  Comparator #(.width(3)) comparator_3 (.a(bitselector_3_out), .b(3'b010), .eq(comparator_3_eq));  // open: gt, lt
  Comparator #(.width(3)) comparator_4 (.a(bitselector_3_out), .b(3'b100), .eq(comparator_4_eq));  // open: gt, lt
  assign bit_extender_7_out = {{2{comparator_4_eq}}, comparator_4_eq};  // Bit_Extender bit_extender_7
  assign bit_extender_8_out = {{29{out_10[2]}}, out_10};  // Bit_Extender bit_extender_8
  assign bit_extender_9_out = {{24{not_2_out[7]}}, not_2_out};  // Bit_Extender bit_extender_9
  or or_2 (or_2_out, comparator_1_eq, comparator_2_eq, comparator_3_eq);
  assign bit_extender_10_out = {{3{comparator_3_eq}}, comparator_3_eq};  // Bit_Extender bit_extender_10
  assign bit_extender_11_out = {{3{comparator_4_eq}}, comparator_4_eq};  // Bit_Extender bit_extender_11
  Comparator #(.width(5)) comparator_5 (
    .a({bitselector_3_out, bitselector_10_out[4:3]}), .b(5'b01110), .eq(comparator_5_eq));  // open: gt, lt
  or or_3 (or_3_out, comparator_5_eq, comparator_6_eq);
  Comparator #(.width(5)) comparator_6 (
    .a({bitselector_3_out, bitselector_10_out[4:3]}), .b(5'b01100), .eq(comparator_6_eq));  // open: gt, lt
  Comparator #(.width(5)) comparator_7 (
    .a({bitselector_3_out, bitselector_10_out[4:3]}), .b(5'b01101), .eq(comparator_7_eq));  // open: gt, lt
  Comparator #(.width(5)) comparator_8 (
    .a({bitselector_3_out, bitselector_10_out[4:3]}), .b(5'b01111), .eq(comparator_8_eq));  // open: gt, lt
  assign and_7_out = bit_extender_6_out & bitselector_6_out;  // AND_Gate and_7, 3 bits wide
  assign and_8_out = bit_extender_7_out & bitselector_10_out[4:2];  // AND_Gate and_8, 3 bits wide
  assign or_4_out = and_4_out | and_1_out;  // OR_Gate or_4, 3 bits wide
  assign bit_extender_12_out = {{3{comparator_1_eq}}, comparator_1_eq};  // Bit_Extender bit_extender_12
  assign bit_extender_13_out = {{3{comparator_2_eq}}, comparator_2_eq};  // Bit_Extender bit_extender_13
  assign bit_extender_14_out = {{3{or_3_out}}, or_3_out};  // Bit_Extender bit_extender_14
  or or_5 (or_5_out, comparator_7_eq, comparator_8_eq);
  assign out_20 = bit_extender_8_out | bit_extender_9_out;  // OR_Gate or_6, 32 bits wide
  assign out_3 = 4'b0010 & bit_extender_12_out;  // AND_Gate and_9, 4 bits wide
  assign out_4 = 4'b0011 & bit_extender_13_out;  // AND_Gate and_10, 4 bits wide
  assign out_5 = 4'b0100 & bit_extender_10_out;  // AND_Gate and_11, 4 bits wide
  assign out_6 = 4'b1001 & bit_extender_11_out;  // AND_Gate and_12, 4 bits wide
  assign bit_extender_15_out = {{3{or_5_out}}, or_5_out};  // Bit_Extender bit_extender_15
  assign out_7 = 4'b0101 & bit_extender_14_out;  // AND_Gate and_13, 4 bits wide
  assign out_8 = 4'b0110 & bit_extender_15_out;  // AND_Gate and_14, 4 bits wide
  assign or_7_out = and_7_out | and_8_out;  // OR_Gate or_7, 3 bits wide
  assign bit_extender_16_out = {{4{or_2_out}}, or_2_out};  // Bit_Extender bit_extender_16
  assign bit_extender_17_out = {{2{or_2_out}}, or_2_out};  // Bit_Extender bit_extender_17
  assign or_8_out = out_3 | out_4 | out_5 | out_6 | out_7 | out_8;  // OR_Gate or_8, 4 bits wide
  assign out_11 = or_8_out & bit_extender_3_out;  // AND_Gate and_15, 4 bits wide
  and and_16 (out_14, or_5_out, in_2);
  assign out_16 = or_4_out & bit_extender_2_out;  // AND_Gate and_17, 3 bits wide
  assign out_17 = out_9 & bit_extender_2_out;  // AND_Gate and_18, 3 bits wide
  assign out_18 = bit_extender_2_out & or_7_out;  // AND_Gate and_19, 3 bits wide
  assign out_19 = bit_extender_4_out & and_5_out;  // AND_Gate and_20, 5 bits wide
  or or_9 (or_9_out, comparator_6_eq, comparator_7_eq);
  or or_10 (or_10_out, comparator_5_eq, comparator_8_eq);
  assign bit_extender_18_out = {{2{or_9_out}}, or_9_out};  // Bit_Extender bit_extender_18
  assign bit_extender_19_out = {{2{or_10_out}}, or_10_out};  // Bit_Extender bit_extender_19
  or or_11 (out_15, or_10_out, comparator_4_eq);

  // Notes on the sheet:
  //   Pull output low on Enable = 0
  //   Note: ALU uses Rn register for shifts. Use Rn instead of Rm for shifts (immediate) here too
  //   Note 2: MOV uses RSB ALU opcode with Imm8 reversed so that it is copied to output register
  //   Note 3: Imm32_Enable forces the use of the immediate for Rm register
  //   Enable carry for SUB since it is reversed in ALU
  //   ALU will use Imm32 instead of Rm
endmodule
